// Logisim project lifebox-alert-logic.circ as structural Verilog: 1 circuit, main circuit main
// LifeBox 2050 - Memoria Sequencial de Alerta
module main (
  input  TRANSPORTE_ATIVO,
  input  TEMPERATURA_CRITICA,
  input  IMPACTO_CRITICO,
  input  RESET,
  output ALERTA,
  output LED,
  output BUZZER
);

  wire clock_1_out, CONDICAO_CRITICA_out, D_out, EVENTO_CRITICO_out;

  or CONDICAO_CRITICA (CONDICAO_CRITICA_out, TEMPERATURA_CRITICA, IMPACTO_CRITICO);
  and EVENTO_CRITICO (EVENTO_CRITICO_out, TRANSPORTE_ATIVO, CONDICAO_CRITICA_out);
  Clock clock_1 (.out(clock_1_out));
  or D (D_out, EVENTO_CRITICO_out, ALERTA);
  D_Flip_Flop MEMORIA_DE_ALERTA (.D(D_out), .clk(clock_1_out), .Q(ALERTA), .reset(RESET));  // open: Qn, preset

  assign BUZZER = ALERTA;
  assign LED = ALERTA;
endmodule
